// Logisim project !.circ as structural Verilog: 2 circuits, main circuit 1bitALU
module _1bitALU (
  input  sub,
  input  cin,
  input  [2:0] opinput,
  input  A,
  input  B,
  input  less,
  output result,
  output Cout,
  output Set
);

  wire and_1_out, nor_1_out, or_1_out, xor_1_out, xor_2_out;

  xor xor_1 (xor_1_out, B, sub);
  and and_1 (and_1_out, A, B);
  or or_1 (or_1_out, A, B);
  xor xor_2 (xor_2_out, A, B);
  nor nor_1 (nor_1_out, A, B);
  Adder #(.width(1)) adder_1 (.a(A), .b(xor_1_out), .out(Set), .cin(cin), .cout(Cout));
  Multiplexer #(.select(3), .enable("false")) multiplexer_1 (
    .in0(and_1_out), .in1(or_1_out), .in2(xor_2_out), .in3(nor_1_out), .in4(Set), .in5(less), .out(result),
    .sel(opinput));  // open: in6, in7

  // Notes on the sheet:
  //   Alu operations-AND,OR,XOR,NOR,ADD/SUB
endmodule

module ALU (
  input  [7:0] A,
  input  sub,
  input  [2:0] op,
  input  [7:0] B,
  output [7:0] R,
  output zero
);

  wire n1bitalu_1_cout, n1bitalu_2_cout, n1bitalu_3_cout, n1bitalu_4_cout, n1bitalu_5_cout, n1bitalu_6_cout,
       n1bitalu_7_cout, n1bitalu_8_set;

  _1bitALU u_1bitalu_1 (
    .A(A[0]), .B(B[0]), .less(n1bitalu_8_set), .result(R[7]), .sub(sub), .cin(sub), .opinput(op),
    .Cout(n1bitalu_1_cout));  // open: Set
  _1bitALU u_1bitalu_2 (
    .A(A[1]), .B(B[1]), .less(1'b0), .result(R[7]), .sub(sub), .cin(n1bitalu_1_cout), .opinput(op),
    .Cout(n1bitalu_2_cout));  // open: Set
  _1bitALU u_1bitalu_3 (
    .A(A[2]), .B(B[2]), .less(1'b0), .result(R[7]), .sub(sub), .cin(n1bitalu_2_cout), .opinput(op),
    .Cout(n1bitalu_3_cout));  // open: Set
  _1bitALU u_1bitalu_4 (
    .A(A[3]), .B(B[3]), .less(1'b0), .result(R[7]), .sub(sub), .cin(n1bitalu_3_cout), .opinput(op),
    .Cout(n1bitalu_4_cout));  // open: Set
  _1bitALU u_1bitalu_5 (
    .A(A[4]), .B(B[4]), .less(1'b0), .result(R[7]), .sub(sub), .cin(n1bitalu_4_cout), .opinput(op),
    .Cout(n1bitalu_5_cout));  // open: Set
  _1bitALU u_1bitalu_6 (
    .A(A[5]), .B(B[5]), .less(1'b0), .result(R[7]), .sub(sub), .cin(n1bitalu_5_cout), .opinput(op),
    .Cout(n1bitalu_6_cout));  // open: Set
  _1bitALU u_1bitalu_7 (
    .A(A[6]), .B(B[6]), .less(1'b0), .result(R[7]), .sub(sub), .cin(n1bitalu_6_cout), .opinput(op),
    .Cout(n1bitalu_7_cout));  // open: Set
  _1bitALU u_1bitalu_8 (
    .A(A[7]), .B(B[7]), .less(1'b0), .result(R[7]), .sub(sub), .cin(n1bitalu_7_cout), .opinput(op),
    .Set(n1bitalu_8_set));  // open: Cout
  nor nor_1 (zero, R[7], R[7], R[7], R[7], R[7], R[7], R[7], R[7]);

  assign R[6:0] = {7{R[7]}};
endmodule
